# Fritzing sketch ReverseMotor3Phaze_6 (saved by Fritzing 0.9.3b)
circuit board: 10cm x 7.5cm
breadboards: 1

parts:
  White = Header 1 [package=1x01_offset]
  R2 = MyDPDT [package=relay-12v]
  AC2 = Header 1 [package=1x01_offset]
  Q1 = NPN-Transistor KT315 [package=KT-13]
  Ground = Header 1 [package=1x01_offset]
  100 = Resistor [tolerance=±5% resistance=100 package=THT]
  4_7K = Resistor [tolerance=±5% resistance=4.7k package=THT]
  2_2K = Resistor [tolerance=±5% resistance=2.2k package=THT]
  20K = Resistor [tolerance=±5% resistance=220 package=THT]
  Blue = Header 1 [package=1x01_offset]
  D2 = Rectifier Diode [part_number=1N4001 package="300 mil [THT]"]
  AC1 = Header 1 [package=1x01_offset]
  Brown = Header 1 [package=1x01_offset]
  C1 = Header 1 [package=1x01_offset]
  C1_2 = Header 1 [package=1x01_offset]
  AC1_2 = Header 1 [package=1x01_offset]
  Nano = Arduino Nano (Rev3.0) (ICSP)
  +12V = Header 1 [package=1x01_offset]
  4_7K_2 = Resistor [tolerance=±5% resistance=4.7k package=THT]
  Ground_2 = Header 1 [package=1x01_offset]
  +12V_2 = Header 1 [package=1x01_offset]
  U3 = TRIAC [package=to-220]
  MOC3020M = MOC3031-M [package=dil06]
  220 = Resistor [tolerance=±5% resistance=220 package=THT]
  Ground_3 = Header 1 [package=1x01_offset]
  1µF = Electrolytic Capacitor [capacitance=1µF voltage=50V package="200 mil [THT, electrolytic]"]
  J1 = screw terminal, 2 pins
  1µF_2 = Electrolytic Capacitor [capacitance=1µF package="200 mil [THT, electrolytic]"]
  20K_2 = Resistor [tolerance=±5% resistance=220 package=THT]
  J2 = screw terminal, 2 pins
  AC2_2 = Header 1 [package=1x01_offset]

nets:
  N1: White.1, R2.pin_4, R2.pin_5, C1.1
  N2: R2.pin_1, D2.cathode, Nano.VIN, +12V.1, 4_7K_2.Pin_0, +12V_2.1
  N3: R2.pin_2, R2.pin_7, Blue.1, C1_2.1
  N4: R2.pin_3, R2.pin_6, U3.MT1
  N5: R2.pin_8, Q1.C, D2.anode
  N6: AC2.1, U3.MT2, 220.Pin_0, AC2_2.1
  N7: Q1.E, Ground.1, 2_2K.Pin_1, 20K.Pin_0, Nano.GND, Ground_2.1, MOC3020M.2, Ground_3.1, 1µF.-, 1µF_2.-, 20K_2.Pin_0
  N8: Q1.B, 4_7K.Pin_1
  N9: 100.Pin_0, Nano.D4
  N10: 100.Pin_1, MOC3020M.1
  N11: 4_7K.Pin_0, Nano.D11/MOSI
  N12: 2_2K.Pin_0, 4_7K_2.Pin_1, J1.pin2, J2.pin2
  N13: 20K.Pin_1, Nano.A0, 1µF.+, J1.pin1
  N14: AC1.1, Brown.1, AC1_2.1
  N15: Nano.A1, 1µF_2.+, 20K_2.Pin_1, J2.pin1
  N16: U3.G, MOC3020M.4
  N17: MOC3020M.6, 220.Pin_1

notes:
  +

custom parts:
  MyDPDT: DPDT Relay - 2 Form C
  NPN-Transistor KT315: A standard NPN-transistor
  TRIAC: Generic TRIAC, TO-220 package
